# Fritzing sketch audio_amplifier_lm386 (saved by Fritzing 0.8.5b)
breadboards: 1

parts:
  U1 = LM386 [package=dip08]
  C1 = Electrolytic Capacitor [capacitance=10µF voltage=16V package="100 mil [THT, electrolytic]"]
  C2 = Ceramic Capacitor [capacitance=100nF voltage=50V package="100 mil [THT, multilayer]"]
  R1 = Resistor [tolerance=±5% resistance=10 package=THT]
  C3 = Electrolytic Capacitor [capacitance=0.22mF voltage=16V package="100 mil [THT, electrolytic]"]
  R2 = Resistor [tolerance=±5% resistance=10k package=THT]
  Speaker_4_to_16ohm = Loudspeaker
  VCC1 = Battery block 9V
  3_5mm_Audio_Jack = 3.5mm Audio Jack [package=audio-jack-3.5mm-smd]

nets:
  N1: U1.GAIN, C1.-, C1.+
  N2: U1.-IN, U1.V-, C2.1, R2.Pin_1, Speaker_4_to_16ohm.pin2, VCC1.-, 3_5mm_Audio_Jack.LEFT
  N3: U1.+IN, R2.Pin_0, 3_5mm_Audio_Jack.RIGHT
  N4: U1.OUT, R1.Pin_0, C3.-
  N5: U1.V+, VCC1.+
  N6: C2.0, R1.Pin_1
  N7: C3.+, Speaker_4_to_16ohm.pin1

notes:
  Sources used:
  http://www.youtube.com/watch?v=3KyBrAoHMX8
  http://tymkrs.tumblr.com/post/6623448606/lm386-audio-amplifier-the-major-components
  http://www.ti.com/lit/gpn/lm386 (LM386 datasheet)
