# Fritzing sketch motor_controllers_l293d (saved by Fritzing 0.8.5b)
breadboards: 1

parts:
  Raspberry_Pi_B_rev1 = Raspberry Pi B rev2
  VCC1 = Battery
  IC1 = L293D [package=THT]
  IC2 = L293D [package=THT]
  R1 = Resistor [tolerance=±5% resistance=10k package=THT]
  R2 = Resistor [tolerance=±5% resistance=10k package=THT]
  M1 = DC Motor
  M2 = DC Motor

nets:
  N1: Raspberry_Pi_B_rev1.5V, IC1.+V, IC2.+V, R1.Pin_0, R2.Pin_0
  N2: Raspberry_Pi_B_rev1.GND, VCC1.-, IC1.0V, IC2.0V
  N3: Raspberry_Pi_B_rev1.GPIO_23, IC2.In_2
  N4: Raspberry_Pi_B_rev1.GPIO_17, IC1.In_1
  N5: Raspberry_Pi_B_rev1.GPIO_18, IC1.In_2
  N6: Raspberry_Pi_B_rev1.GPIO_22, IC2.In_1
  N7: VCC1.+, IC1.+Vmotor, IC2.+Vmotor
  N8: IC1.Enable_1, R1.Pin_1
  N9: IC1.Out_1_(_Controlled_by_Enable_1_), M1.pin_1
  N10: IC1.Out_2_(_Controlled_by_Enable_1_), M1.pin_2
  N11: IC2.Enable_1, R2.Pin_1
  N12: IC2.Out_1_(_Controlled_by_Enable_1_), M2.pin_1
  N13: IC2.Out_2_(_Controlled_by_Enable_1_), M2.pin_2
