# Fritzing sketch motor_controllers_l293d_impl (saved by Fritzing 0.8.7b)
breadboards: 1

parts:
  M1 = DC Motor
  Raspberry_Pi_B_rev1 = Raspberry Pi B rev2
  VCC1 = Battery
  IC1 = L293D [package=THT]
  R1 = Resistor [tolerance=±5% resistance=10k package=THT]

nets:
  N1: M1.pin_1, IC1.Out_2_(_Controlled_by_Enable_1_)
  N2: M1.pin_2, IC1.Out_1_(_Controlled_by_Enable_1_)
  N3: Raspberry_Pi_B_rev1.5V, IC1.+V, R1.Pin_0
  N4: Raspberry_Pi_B_rev1.GND, VCC1.-, IC1.0V
  N5: Raspberry_Pi_B_rev1.GPIO_17, IC1.In_1
  N6: Raspberry_Pi_B_rev1.GPIO_18, IC1.In_2
  N7: VCC1.+, IC1.+Vmotor
  N8: IC1.Enable_1, R1.Pin_1
